// Logisim project cpu.circ as structural Verilog: 1 circuit, main circuit main
module main (
  output out_1,
  output [7:0] out_2,
  output [7:0] out_3,
  output [3:0] out_4,
  output [1:0] out_5,
  output [1:0] out_6,
  output [7:0] RegData1,
  output [1:0] out_8,
  output [1:0] out_9,
  output [1:0] out_10,
  output [7:0] out_11,
  output [5:0] out_12,
  output [7:0] out_13,
  output [1:0] out_14,
  output [7:0] out_15,
  output [7:0] RegData2,
  output [7:0] out_17,
  output [7:0] out_18,
  output [7:0] RegDataW,
  output [7:0] out_20,
  output out_21,
  output out_22,
  output out_23,
  output out_24,
  output out_25
);

  wire and_1_out, and_3_out, and_4_out, and_5_out, and_6_out, clock_1_out, clock_2_out, decoder_1_out0,
       decoder_1_out1, decoder_1_out2, decoder_1_out3, not_1_out, not_3_out, undriven;
  wire [7:0] adder_1_out, multiplexer_5_out, PC_q, X0_q, X1_q, X2_q, X3_q;

  Clock #(.highDuration(2), .lowDuration(2)) clock_1 (.out(clock_1_out));
  Register PC (.D(adder_1_out), .en(1'b1), .clk(clock_1_out), .Q(PC_q), .clr(undriven));
  Adder adder_1 (.a(PC_q), .b(8'h1), .out(adder_1_out));  // open: cin, cout
  RAM ram_1 (
    .addr(PC_q), .we(1'b0), .oe(1'b1), .clk(clock_1_out), .dout({out_1, out_14[0], out_9, out_4}));  // open: din
  Clock clock_2 (.out(clock_2_out));
  RAM #(.addrWidth(4)) ram_2 (
    .addr(out_4), .we(and_1_out), .oe(not_1_out), .clk(clock_2_out), .din(out_20), .dout(out_2));
  not not_1 (not_1_out, and_1_out);
  and and_1 (and_1_out, out_14[0], out_1);
  or or_1 (out_24, out_14[0], out_14[0]);
  and and_2 (out_25, out_14[0], 1'b1);
  Multiplexer #(.width(8)) multiplexer_1 (.in0(out_2), .in1(multiplexer_5_out), .out(out_3), .sel(out_25));
  Decoder #(.select(2)) decoder_1 (
    .out0(decoder_1_out0), .out1(decoder_1_out1), .out2(decoder_1_out2), .out3(decoder_1_out3), .sel(out_9),
    .en(1'b1));
  not not_2 (out_21, and_1_out);
  and and_3 (and_3_out, decoder_1_out0, out_21);
  and and_4 (and_4_out, decoder_1_out1, out_21);
  and and_5 (and_5_out, decoder_1_out2, out_21);
  and and_6 (and_6_out, decoder_1_out3, out_21);
  Register X0 (.D(out_3), .en(and_3_out), .clk(clock_1_out), .Q(X0_q));  // open: clr
  Register X1 (.D(out_3), .en(and_4_out), .clk(clock_1_out), .Q(X1_q));  // open: clr
  Register X2 (.D(out_3), .en(and_5_out), .clk(clock_1_out), .Q(X2_q));  // open: clr
  Register X3 (.D(out_3), .en(and_6_out), .clk(clock_1_out), .Q(X3_q));  // open: clr
  Multiplexer #(.select(2), .width(8)) multiplexer_2 (
    .in0(X0_q), .in1(X1_q), .in2(X2_q), .in3(X3_q), .out(out_15), .sel(out_4[3:2]));
  Multiplexer #(.select(2), .width(8)) multiplexer_3 (
    .in0(X0_q), .in1(X1_q), .in2(X2_q), .in3(X3_q), .out(out_13), .sel(out_4[1:0]));
  Multiplexer #(.select(2), .width(8)) multiplexer_4 (
    .in0(X0_q), .in1(X1_q), .in2(X2_q), .in3(X3_q), .out(out_20), .sel(out_9));
  Adder adder_2 (.a(out_15), .b(out_13), .out(out_11));  // open: cin, cout
  Subtractor subtractor_1 (.a(out_15), .b(out_13), .out(out_18));  // open: bin, bout
  not not_3 (not_3_out, out_1);
  Multiplexer #(.width(8)) multiplexer_5 (.in0(out_11), .in1(out_18), .out(multiplexer_5_out), .sel(not_3_out));

  assign out_5 = out_4[3:2];
  assign out_6 = out_4[1:0];
  assign out_8 = out_4[3:2];
  assign out_10 = out_4[1:0];
  assign out_12 = {out_9, out_4};
  assign out_14[1] = out_1;
  assign out_17 = {out_1, out_14[0], out_9, out_4};
  assign out_22 = out_14[0];
  assign out_23 = out_1;
  assign RegData1 = out_15;
  assign RegData2 = out_13;
  assign RegDataW = out_3;

  // Notes on the sheet:
  //   I pledge my honor that I have abided by the Stevens Honor System.
  //   Sarang Hadagali and Dev Patel
  //   Write Port
  //   RegWrite
  //   00 sub
  //   01 add
  //   10 ldr
  //   11 str
  //   nvm- adding store might be annoying
  //   need another mux or read port to read reg for str b/c different spot then other instructions
  //   not sure if this str works all g
  //   need mux here to choose to send to ldr or str
  //   have and gate w 1 and value depending on which one
  //   Read Ports
endmodule
