// Logisim project cpu2.circ as structural Verilog: 1 circuit, main circuit main
module main (
  input  [1:0] WriteReg,
  input  RegWrite,
  output out_3,
  output out_4,
  output [7:0] out_5,
  output [1:0] out_6,
  output [7:0] RegData1,
  output [1:0] out_8,
  output [1:0] out_9,
  output [1:0] out_10,
  output [7:0] out_11,
  output [7:0] out_12,
  output [7:0] RegData2
);

  wire and_1_out, and_2_out, and_3_out, and_4_out, clock_1_out, decoder_1_out0, decoder_1_out1,
       decoder_1_out2, decoder_1_out3, multiplexer_1_out, undriven;
  wire [7:0] adder_1_out, PC_q, ram_2_dout, X1_q, X2_q, X3_q, X4_q;

  Clock clock_1 (.out(clock_1_out));
  Register PC (.D(adder_1_out), .en(1'b1), .clk(clock_1_out), .Q(PC_q), .clr(undriven));
  Adder adder_1 (.a(PC_q), .b(8'h1), .out(adder_1_out));  // open: cin, cout
  RAM ram_1 (
    .addr(PC_q), .we(1'b0), .oe(1'b1), .clk(clock_1_out), .dout({out_4, out_3, out_8, out_9, out_10}));  // open: din
  RAM #(.addrWidth(2)) ram_2 (
    .addr({out_4, out_3}), .we(1'b0), .oe(1'b1), .clk(clock_1_out), .dout(ram_2_dout));  // open: din
  Multiplexer #(.select(2)) multiplexer_1 (.out(multiplexer_1_out));  // open: in0, in1, in2, in3, sel
  Decoder #(.select(2)) decoder_1 (
    .out0(decoder_1_out0), .out1(decoder_1_out1), .out2(decoder_1_out2), .out3(decoder_1_out3), .sel(out_8),
    .en(1'b1));
  and and_1 (and_1_out, decoder_1_out0, RegWrite);
  and and_2 (and_2_out, decoder_1_out1, RegWrite);
  and and_3 (and_3_out, decoder_1_out2, RegWrite);
  and and_4 (and_4_out, decoder_1_out3, RegWrite);
  Register X1 (.D(ram_2_dout), .en(and_1_out), .clk(clock_1_out), .Q(X1_q));  // open: clr
  Register X2 (.D(ram_2_dout), .en(and_2_out), .clk(clock_1_out), .Q(X2_q));  // open: clr
  Register X3 (.D(ram_2_dout), .en(and_3_out), .clk(clock_1_out), .Q(X3_q));  // open: clr
  Register X4 (.D(ram_2_dout), .en(and_4_out), .clk(clock_1_out), .Q(X4_q));  // open: clr
  Multiplexer #(.select(2), .width(8)) multiplexer_2 (
    .in0(X1_q), .in1(X2_q), .in2(X3_q), .in3(X4_q), .out(RegData1), .sel(out_9));
  Multiplexer #(.select(2), .width(8)) multiplexer_3 (
    .in0(X1_q), .in1(X2_q), .in2(X3_q), .in3(X4_q), .out(RegData2), .sel(out_10));
  Adder adder_2 (.a(RegData1), .b(RegData2), .out(out_11));  // open: cin, cout
  Subtractor subtractor_1 (.a(RegData1), .b(RegData2), .out(out_12));  // open: bin, bout
  Multiplexer #(.width(8)) multiplexer_4 (.in0(out_11), .in1(out_12), .out(out_5), .sel(out_3));

  assign out_6 = {out_4, out_3};

  // Notes on the sheet:
  //   Write Port
  //   00 add
  //   01 sub
  //   10 ldr
  //   11 str
  //   Read Ports
endmodule
