// Logisim project project2.circ as structural Verilog: 4 circuits, main circuit main
module main (
);

  wire Ram_Clock_out;
  wire [7:0] adder_1_out, RAM_Unit_dout, Register_tracks_memory_q;

  Clock Ram_Clock (.out(Ram_Clock_out));
  Adder adder_1 (.a(Register_tracks_memory_q), .b(8'h1), .out(adder_1_out));  // open: cin, cout
  Register Register_tracks_memory (
    .D(adder_1_out), .clk(Ram_Clock_out), .Q(Register_tracks_memory_q));  // open: en, clr
  RAM RAM_Unit (
    .addr(Register_tracks_memory_q), .we(1'b0), .oe(1'b1), .clk(Ram_Clock_out), .dout(RAM_Unit_dout));  // open: din
  adding adding_1 ();  // open: in_1, inputA, inputB, AplusB, CarryOut
  miniReg minireg_1 ();  // open: WriteReg, RegWrite, RegDataW, ReadReg1, ReadReg2, Output1, Output2

  // Notes on the sheet:
  //   Sarang Hadagali and Dev Patel
  //   I pledge my honor that I have abided by the Stevens Honor System
  //   Ram Unit
endmodule

module miniReg (
  input  [1:0] WriteReg,
  input  RegWrite,
  input  [7:0] RegDataW,
  input  [1:0] ReadReg1,
  input  [1:0] ReadReg2,
  output [7:0] Output1,
  output [7:0] Output2
);

  wire and_1_out, and_2_out, and_3_out, and_4_out, decoder_1_out0, decoder_1_out1, decoder_1_out2,
       decoder_1_out3, RegisterClock_out;
  wire [7:0] RegisterA_q, RegisterB_q, RegisterC_q, RegisterD_q;

  Clock RegisterClock (.out(RegisterClock_out));
  Decoder #(.select(2)) decoder_1 (
    .out0(decoder_1_out0), .out1(decoder_1_out1), .out2(decoder_1_out2), .out3(decoder_1_out3),
    .sel(WriteReg), .en(1'b1));
  and and_1 (and_1_out, decoder_1_out0, RegWrite);
  and and_2 (and_2_out, decoder_1_out1, RegWrite);
  and and_3 (and_3_out, decoder_1_out2, RegWrite);
  and and_4 (and_4_out, decoder_1_out3, RegWrite);
  Register RegisterA (.D(RegDataW), .en(and_1_out), .clk(RegisterClock_out), .Q(RegisterA_q));  // open: clr
  Register RegisterB (.D(RegDataW), .en(and_2_out), .clk(RegisterClock_out), .Q(RegisterB_q));  // open: clr
  Register RegisterC (.D(RegDataW), .en(and_3_out), .clk(RegisterClock_out), .Q(RegisterC_q));  // open: clr
  Register RegisterD (.D(RegDataW), .en(and_4_out), .clk(RegisterClock_out), .Q(RegisterD_q));  // open: clr
  Multiplexer #(.select(2), .width(8)) multiplexer_1 (
    .in0(RegisterA_q), .in1(RegisterB_q), .in2(RegisterC_q), .in3(RegisterD_q), .out(Output1), .sel(ReadReg1));
  Multiplexer #(.select(2), .width(8)) multiplexer_2 (
    .in0(RegisterA_q), .in1(RegisterB_q), .in2(RegisterC_q), .in3(RegisterD_q), .out(Output2), .sel(ReadReg2));
endmodule

module instructionMem (
  output [7:0] outbits
);

  wire Ram_Clock_out;
  wire [7:0] adder_1_out, Register_tracks_memory_q;

  Clock Ram_Clock (.out(Ram_Clock_out));
  Adder adder_1 (.a(Register_tracks_memory_q), .b(8'h1), .out(adder_1_out));  // open: cin, cout
  Register Register_tracks_memory (
    .D(adder_1_out), .clk(Ram_Clock_out), .Q(Register_tracks_memory_q));  // open: en, clr
  RAM RAM_Unit (
    .addr(Register_tracks_memory_q), .we(1'b0), .oe(1'b1), .clk(Ram_Clock_out), .dout(outbits));  // open: din

  // Notes on the sheet:
  //   Ram Unit
endmodule

module adding (
  input  in_1,
  input  [3:0] inputA,
  input  [3:0] inputB,
  output [3:0] AplusB,
  output CarryOut
);

  wire A_out, and_1_out, and_2_out, and_3_out, and_4_out, and_5_out, and_6_out, and_7_out, and_8_out,
       and_9_out, C_out, D_out, E_out, F_out, or_2_out, or_3_out, xor_1_out, xor_2_out, xor_3_out;

  xor xor_1 (xor_1_out, or_3_out, inputA[3]);
  and and_1 (and_1_out, or_3_out, inputB[3]);
  and and_2 (and_2_out, or_3_out, inputA[3]);
  and and_3 (and_3_out, inputA[3], inputB[3]);
  xor A (A_out, in_1, inputA[0]);
  and C (C_out, in_1, inputB[0]);
  and D (D_out, inputA[0], in_1);
  and E (E_out, inputA[0], inputB[0]);
  xor xor_2 (xor_2_out, F_out, inputA[1]);
  and and_4 (and_4_out, F_out, inputB[1]);
  and and_5 (and_5_out, inputA[1], F_out);
  and and_6 (and_6_out, inputA[1], inputB[1]);
  xor xor_3 (xor_3_out, or_2_out, inputA[2]);
  and and_7 (and_7_out, or_2_out, inputB[2]);
  and and_8 (and_8_out, inputA[2], or_2_out);
  and and_9 (and_9_out, inputA[2], inputB[2]);
  xor xor_4 (AplusB[3], xor_1_out, inputB[3]);
  or or_1 (CarryOut, and_1_out, and_2_out, and_3_out);
  xor B (AplusB[0], A_out, inputB[0]);
  xor xor_5 (AplusB[1], xor_2_out, inputB[1]);
  or or_2 (or_2_out, and_4_out, and_5_out, and_6_out);
  xor xor_6 (AplusB[2], xor_3_out, inputB[2]);
  or or_3 (or_3_out, and_7_out, and_8_out, and_9_out);
  or F (F_out, C_out, D_out, E_out);

  // Notes on the sheet:
  //   The carry output here is the final carryout, that shows whether or not there would be some overflow error.
endmodule
