// Logisim project sar1cpu.circ as structural Verilog: 1 circuit, main circuit main
module main (
  output [7:0] out_1,
  output [7:0] out_2,
  output [3:0] out_3,
  output [1:0] out_4,
  output [1:0] out_5,
  output [7:0] RegData1,
  output [7:0] out_7,
  output [1:0] out_8,
  output [1:0] out_9,
  output [1:0] out_10,
  output [5:0] out_11,
  output [7:0] out_12,
  output [7:0] out_13,
  output [1:0] out_14,
  output out_15,
  output [7:0] out_16,
  output [7:0] RegData2,
  output [7:0] out_18,
  output [7:0] RegDataW,
  output [7:0] out_20,
  output out_21,
  output out_22,
  output out_23
);

  wire and_1_out, and_2_out, and_3_out, and_4_out, and_5_out, clock_1_out, clock_2_out, decoder_1_out0,
       decoder_1_out1, decoder_1_out2, decoder_1_out3, not_1_out, not_4_out, undriven;
  wire [7:0] adder_1_out, PC_q, subtractor_1_out, X0_q, X1_q, X2_q, X3_q;

  Register PC (.D(adder_1_out), .en(1'b1), .clk(clock_1_out), .Q(PC_q), .clr(undriven));
  Adder adder_1 (.a(PC_q), .b(8'h1), .out(adder_1_out));  // open: cin, cout
  Clock #(.highDuration(2), .lowDuration(2)) clock_1 (.out(clock_1_out));
  RAM ram_1 (.addr(PC_q), .we(1'b0), .oe(1'b1), .clk(clock_1_out), .dout({out_14, out_9, out_3}));  // open: din
  Clock clock_2 (.out(clock_2_out));
  RAM #(.addrWidth(4)) ram_2 (
    .addr(out_3), .we(and_1_out), .oe(not_1_out), .clk(clock_2_out), .din(out_20), .dout(out_1));
  not not_1 (not_1_out, and_1_out);
  not not_2 (out_15, out_14[1]);
  and and_1 (and_1_out, out_14[0], out_14[1]);
  Multiplexer #(.width(8)) multiplexer_1 (.in0(out_1), .in1(out_13), .out(out_2), .sel(out_15));
  Decoder #(.select(2)) decoder_1 (
    .out0(decoder_1_out0), .out1(decoder_1_out1), .out2(decoder_1_out2), .out3(decoder_1_out3), .sel(out_9),
    .en(1'b1));
  not not_3 (out_21, and_1_out);
  not not_4 (not_4_out, out_14[0]);
  and and_2 (and_2_out, decoder_1_out0, out_21);
  and and_3 (and_3_out, decoder_1_out1, out_21);
  and and_4 (and_4_out, decoder_1_out2, out_21);
  and and_5 (and_5_out, decoder_1_out3, out_21);
  Register X0 (.D(out_2), .en(and_2_out), .clk(clock_1_out), .Q(X0_q));  // open: clr
  Register X1 (.D(out_2), .en(and_3_out), .clk(clock_1_out), .Q(X1_q));  // open: clr
  Register X2 (.D(out_2), .en(and_4_out), .clk(clock_1_out), .Q(X2_q));  // open: clr
  Register X3 (.D(out_2), .en(and_5_out), .clk(clock_1_out), .Q(X3_q));  // open: clr
  Multiplexer #(.select(2), .width(8)) multiplexer_2 (
    .in0(X0_q), .in1(X1_q), .in2(X2_q), .in3(X3_q), .out(out_16), .sel(out_3[3:2]));
  Multiplexer #(.select(2), .width(8)) multiplexer_3 (
    .in0(X0_q), .in1(X1_q), .in2(X2_q), .in3(X3_q), .out(out_12), .sel(out_3[1:0]));
  Multiplexer #(.select(2), .width(8)) multiplexer_4 (
    .in0(X0_q), .in1(X1_q), .in2(X2_q), .in3(X3_q), .out(out_20), .sel(out_9));
  Adder adder_2 (.a(out_16), .b(out_12), .out(out_7));  // open: cin, cout
  Subtractor subtractor_1 (.a(out_16), .b(out_12), .out(subtractor_1_out));  // open: bin, bout
  Multiplexer #(.width(8)) multiplexer_5 (.in0(out_7), .in1(subtractor_1_out), .out(out_13), .sel(not_4_out));

  assign out_4 = out_3[3:2];
  assign out_5 = out_3[1:0];
  assign out_8 = out_3[3:2];
  assign out_10 = out_3[1:0];
  assign out_11 = {out_9, out_3};
  assign out_18 = {out_14, out_9, out_3};
  assign out_22 = out_14[0];
  assign out_23 = out_14[1];
  assign RegData1 = out_16;
  assign RegData2 = out_12;
  assign RegDataW = out_2;

  // Notes on the sheet:
  //   I pledge my honor that I have abided by the Stevens Honor System.
  //   Sarang Hadagali and Dev Patel
  //   Write Port
  //   RegWrite
  //   Read Ports
endmodule
